# Fritzing sketch wso2con-rfid (saved by Fritzing 0.8.7b)
circuit board: 8cm x 5.2cm

parts:
  R1 = Resistor [tolerance=±5% resistance=100 package=THT]
  LED1 = LED - 5mm [color="Red (633nm)" package="5 mm [THT]"]
  LED2 = LED - 5mm [color="Green (570nm)" package="5 mm [THT]"]
  R2 = Resistor [tolerance=±5% resistance=100 package=THT]
  J2 = female pin header, 8 pins [form="♀ (female)"]
  SG1 = Buzzer 12mm [package=buzzer-12mm]
  RaspberryPi1 = Raspberry Pi Model B

nets:
  N1: R1.Pin_0, RaspberryPi1.#17
  N2: R1.Pin_1, LED2.anode
  N3: LED1.cathode, LED2.cathode, J2.pin3, SG1.1, RaspberryPi1.GND
  N4: LED1.anode, R2.Pin_1
  N5: R2.Pin_0, RaspberryPi1.#21
  N6: J2.pin1, RaspberryPi1.3V3
  N7: J2.pin2, RaspberryPi1.#25
  N8: J2.pin5, RaspberryPi1.MISO
  N9: J2.pin6, RaspberryPi1.MOSI
  N10: J2.pin7, RaspberryPi1.SCLK
  N11: J2.pin8, RaspberryPi1.CS0
  N12: SG1.2, RaspberryPi1.#4

notes:
  RFID Shield v1.0 (c) 2014

custom parts:
  Raspberry Pi Model B: Raspberry Pi (Model B)
